# Fritzing sketch schematic (saved by Fritzing 0.9.3b)

parts:
  Part1 = Arduino Uno (Rev3)
  microSD1 = MicroSD Card Module
  U1 = GP-2106 [package=gp-2106]

nets:
  N1: Part1.D8, microSD1.CS
  N2: Part1.D11_PWM/MOSI, microSD1.MOSI
  N3: Part1.D12/MISO, microSD1.MISO
  N4: Part1.D13/SCK, microSD1.SCK
  GND: Part1.GND, microSD1.GND, U1.GND
  N5: Part1.D3_PWM, U1.TX
  N6: Part1.D4, U1.RX
  VCC: Part1.5V, microSD1.VCC, U1.VCC
